# Fritzing sketch gibbon-v1128 (saved by Fritzing 0.9.2b)

parts:
  mega = Arduino Mega 2560 (Rev3)  # not connected
  mega_shield = Arduino Mega Proto Shield (v6)
  IC1 = H-Bridge [package=THT]
  IC2 = H-Bridge [package=THT]
  IC3 = H-Bridge [package=THT]
  Fan1 = DC Motor  # not connected
  Fan2 = DC Motor  # not connected
  Fan3 = DC Motor  # not connected
  Fan4 = DC Motor  # not connected
  Fan5 = DC Motor  # not connected
  Fan6 = DC Motor  # not connected
  Bubble1 = Basic Servo  # not connected
  Bubble2 = Basic Servo  # not connected
  Bubble3 = Basic Servo  # not connected
  Bubble4 = Basic Servo  # not connected
  Bubble5 = Basic Servo  # not connected
  Bubble6 = Basic Servo  # not connected
  Servo2L = Basic Servo  # not connected
  Servo3R = Basic Servo  # not connected
  Servo3L = Basic Servo  # not connected
  Servo2R = Basic Servo  # not connected
  Servo1L = Basic Servo  # not connected
  Servo1R = Basic Servo  # not connected
  Servo5L = Basic Servo  # not connected
  Servo6R = Basic Servo  # not connected
  Servo6L = Basic Servo  # not connected
  Servo5R = Basic Servo  # not connected
  Servo4L = Basic Servo  # not connected
  Servo4R = Basic Servo  # not connected

nets:
  N1: mega_shield.N$105, IC1.VCC2
  N2: mega_shield.N$186, IC2.VCC1
  N3: mega_shield.N$193, IC2.1_2EN
  N4: mega_shield.N$195, IC3.VCC2
  N5: mega_shield.N$197, IC3.3_4EN
  N6: mega_shield.N$198, IC2.4A
  N7: mega_shield.N$202, IC2.1A
  N8: mega_shield.N$204, IC1.2A
  N9: mega_shield.N$206, IC3.2A
  N10: mega_shield.N$209, IC3.3A
  N11: mega_shield.N$211, IC2.4Y
  N12: mega_shield.N$214, IC2.1Y
  N13: mega_shield.N$215, IC1.2Y
  N14: mega_shield.N$217, IC3.2Y
  N15: mega_shield.N$224, IC3.3Y
  N16: mega_shield.N$226, IC2.GND4
  N17: mega_shield.N$253, IC2.GND1
  N18: mega_shield.N$254, IC1.GND2
  N19: mega_shield.N$256, IC3.GND2
  N20: mega_shield.N$260, IC3.GND3
  N21: mega_shield.N$265, IC2.GND3
  N22: mega_shield.N$287, IC2.GND2
  N23: mega_shield.N$288, IC1.GND1
  N24: mega_shield.N$301, IC3.GND1
  N25: mega_shield.N$306, IC3.GND4
  N26: mega_shield.N$328, IC2.3Y
  N27: mega_shield.N$334, IC2.2Y
  N28: mega_shield.N$337, IC1.1Y
  N29: mega_shield.N$341, IC3.1Y
  N30: mega_shield.N$344, IC3.4Y
  N31: mega_shield.N$346, IC2.3A
  N32: mega_shield.N$349, IC2.2A
  N33: mega_shield.N$350, IC1.1A
  N34: mega_shield.N$352, IC3.1A
  N35: mega_shield.N$386, IC3.4A
  N36: mega_shield.N$388, IC2.3_4EN
  N37: mega_shield.N$391, IC2.VCC2
  N38: mega_shield.N$392, IC1.1_2EN
  N39: mega_shield.N$437, IC3.1_2EN
  N40: mega_shield.N$440, IC3.VCC1
  N41: mega_shield.N$441, IC1.3_4EN
  N42: mega_shield.N$442, IC1.3A
  N43: mega_shield.N$443, IC1.3Y
  N44: mega_shield.N$444, IC1.GND3
  N45: mega_shield.N$445, IC1.GND4
  N46: mega_shield.N$446, IC1.4Y
  N47: mega_shield.N$447, IC1.4A
  N48: mega_shield.N$448, IC1.VCC1
